// Digital circuit contador_soma_sub_m.dig as structural Verilog
module contador_soma_sub_m (
  input  clk,
  output out_2,
  output out_3,
  output [6:0] out_4
);

  wire button_1_out, button_2_out, button_3_out, button_4_out;

  Button button_1 (.out(button_1_out));
  Button button_2 (.out(button_2_out));
  Button button_3 (.out(button_3_out));
  Button button_4 (.out(button_4_out));
  contador_soma_sub_m #(.applicationType("IVERILOG")) u_contador_soma_sub_m (
    .clock(clk), .zera_as(button_1_out), .zera_s(button_2_out), .soma(button_3_out), .sub(button_4_out),
    .Q(out_4), .fim(out_2), .meio(out_3));

  // Notes on the sheet:
  //   clk: Hz: 2
endmodule

/* Code of contador_soma_sub_m:
module contador_soma_sub_m
  (
    input  wire          clock,
    input  wire          zera_as,
    input  wire          zera_s,
    input  wire          soma,
    input  wire          sub,
    output reg  [6:0]  Q,
    output reg           fim,
    output reg           meio
  );

  always @(posedge clock or posedge zera_as) begin
    if (zera_as) begin
      Q <= 0;
    end else if (clock) begin
      if (zera_s) begin
        Q <= 0;
      end else if (soma) begin
        if (Q == 99) begin
          Q <= Q;
        end else begin
          // Q <= Q + 1;
          Q <= Q + 1'b1;
        end
      end
    else if (sub) begin
        if (Q == 0) begin
        Q <= Q;
        end else begin
        // Q <= Q - 1;
        Q <= Q - 1'b1;
        end
    end
    end
  end

  // Saidas
  always @ (Q)
      if (Q == 99)   fim = 1;
      else            fim = 0;

  always @ (Q)
      if (Q == 47) meio = 1;
      else            meio = 0;

endmodule
*/
